// Logisim project main.circ as structural Verilog: 1 circuit, main circuit main
module main (
  input  in_1,
  input  in_2,
  input  in_3,
  input  in_4,
  input  in_5,
  input  in_6,
  input  in_7,
  input  in_8,
  input  in_9,
  input  in_10,
  input  in_11,
  input  in_12,
  input  in_13,
  input  in_14,
  input  in_15,
  output out_16,
  output out_17,
  output out_18,
  output out_19
);

  wire clock_1_out;
  wire [7:0] A_q, B_q;

  Clock clock_1 (.out(clock_1_out));
  Register A (.clk(clock_1_out), .Q(A_q));  // open: D, en, clr
  Register H (.clk(clock_1_out));  // open: D, en, Q, clr
  Register B (.clk(clock_1_out), .Q(B_q));  // open: D, en, clr
  Register L (.clk(clock_1_out));  // open: D, en, Q, clr
  Register C (.clk(clock_1_out));  // open: D, en, Q, clr
  // _74381 74381_1: pin names not known; wires that end beside it: 1'b1, in_9, in_10, in_13, in_14, in_8, in_11, in_12, in_15, in_7, in_1, in_6, in_5, out_16, out_19, out_17, out_18, 1'b0
  Register X (.clk(clock_1_out));  // open: D, en, Q, clr
  Register D (.clk(clock_1_out));  // open: D, en, Q, clr
  Register Z (.clk(clock_1_out));  // open: D, en, Q, clr
  Multiplexer #(.select(3), .width(8)) multiplexer_1 (.in0(A_q));  // open: in1, in2, in3, in4, in5, in6, in7, out, sel
  Multiplexer #(.select(3), .width(8)) multiplexer_2 ();  // open: in0, in1, in2, in3, in4, in5, in6, in7, out, sel
  _74139 u_74139_1 (
    .pin1(in_2), .pin2(in_3), .pin3(in_4));  // open: pin4, pin5, pin6, pin7, pin15, pin14, pin13, pin12, pin11, pin10, pin9
  // _74381 74381_2: pin names not known; wires that end beside it: 1'b1
  // _74381 74381_3: pin names not known; wires that end beside it: 1'b1
  // _74381 74381_4: pin names not known; wires that end beside it: 1'b1
endmodule
